# Fritzing sketch Prototipo_Nodemcu (saved by Fritzing 0.9.3b)
breadboards: 1

parts:
  T2 = LM35 Temperature Sensor [package="TO92 [THT]"]
  GY1 = GY-521 (MPU-6050) [form="♀ (female)" package=THT]
  U1 = NodeMCU V1.0
  TP1 = TP4056 [chip_label=TP4056 package="DIP (Dual Inline) [THT]"]
  U4 = LIPO-2000mAh [package=lipo-2000]
  U5 = Mini-360 DC-DC Buck converter [package=THT]

nets:
  VCC: T2.+Vs, GY1.VCC, U1.3V3
  N1: T2.Vout, U1.A0
  GND: T2.GND, GY1.GND, U1.GND, U5.OUT-
  N2: GY1.SCL, U1.D1
  N3: GY1.SDA, U1.D2
  N4: U1.Vin, U5.OUT+
  N5: TP1.pin3, U5.IN-
  N6: TP1.pin4, U4.+
  N7: TP1.pin5, U4.-
  N8: TP1.pin6, U5.IN+

custom parts:
  GY-521 (MPU-6050): Placa GY-521 basada en conjunto de acelerómetro+giroscopios MPU-6050
  NodeMCU V1.0: ESP8266 based NodeMCU
  TP4056: A DIP stand-in part for whatever IC you want. With 6 pins on a 300mil dual inline package (DIP) footprint.
  Mini-360 DC-DC Buck converter: Mini-360 DC-DC Buck converter. Tiny buck step down voltage converter, input voltage 4.75 to 23V output 1 to 17V adjustable. Available from ebay and the like.
