# Fritzing sketch Prototipo_Nodemcu_SemRTC (saved by Fritzing 0.9.3b)
breadboards: 1

parts:
  Componente2 = MicroSD Card Module
  T2 = LM35 Temperature Sensor [package="TO92 [THT]"]
  U2 = NodeMCU V1.0
  GY2 = GY-521 (MPU-6050) [form="♀ (female)" package=THT]

nets:
  GND: Componente2.GND, T2.GND, U2.GND, GY2.GND
  VCC: Componente2.VCC, U2.Vin, GY2.VCC
  N1: Componente2.MISO, U2.D6
  N2: Componente2.MOSI, U2.D7
  N3: Componente2.SCK, U2.D5
  N4: Componente2.CS, U2.D8
  N5: T2.+Vs, U2.3V3
  N6: T2.Vout, U2.A0
  N7: U2.D1, GY2.SCL
  N8: U2.D2, GY2.SDA

custom parts:
  NodeMCU V1.0: ESP8266 based NodeMCU
  GY-521 (MPU-6050): Placa GY-521 basada en conjunto de acelerómetro+giroscopios MPU-6050
